# Fritzing sketch esquema (saved by Fritzing 0.9.3b)
breadboards: 2

parts:
  Onderdeel2 = Arduino Uno (Rev3)
  LCD2 = LCD screen
  LCM1602_IIC2 = LCM1602 IIC [part_number="LCM1602 IIC" chip_label="LCM1602 IIC" package="DIP (Dual Inline) [THT]"]
  J1 = Piezo Speaker  # not connected
  S1 = Round Pushbutton  # not connected
  Part1 = SCD30  # not connected

nets:
  N1: Onderdeel2.A4/SDA, LCM1602_IIC2.SDA
  N2: Onderdeel2.A5/SCL, LCM1602_IIC2.SCL
  5V: Onderdeel2.5V, LCM1602_IIC2.VCC
  GND: Onderdeel2.GND, LCM1602_IIC2.GND
  VSS: LCD2.VSS, LCM1602_IIC2.VSS
  VDD: LCD2.VDD, LCM1602_IIC2.VDD
  N3: LCD2.V0, LCM1602_IIC2.V0
  N4: LCD2.RS, LCM1602_IIC2.RS
  N5: LCD2.R/W, LCM1602_IIC2.RW
  N6: LCD2.E, LCM1602_IIC2.E
  N7: LCD2.DB0, LCM1602_IIC2.D0
  N8: LCD2.DB1, LCM1602_IIC2.D1
  N9: LCD2.DB2, LCM1602_IIC2.D2
  N10: LCD2.DB3, LCM1602_IIC2.D3
  N11: LCD2.DB4, LCM1602_IIC2.D4
  N12: LCD2.DB5, LCM1602_IIC2.D5
  N13: LCD2.DB6, LCM1602_IIC2.D6
  N14: LCD2.DB7, LCM1602_IIC2.D7
  N15: LCD2.LED+, LCM1602_IIC2.A
  N16: LCD2.LED-, LCM1602_IIC2.K
  N17: LCM1602_IIC2.LED_A, LCM1602_IIC2.LED_B

notes:
  Batería 5V 10000 mAh

custom parts:
  LCM1602 IIC: I2C-Module to use a 1602 or 2004 LCD on with the wire.h libory Serial LCD Modul
  SCD30: CO2 , humidity, and temperature sensor * Current consumption: 19 mA @ 1 meas. per 2 s. * Digital interface UART or I2C * Company: Sensirion - The Sensor Company Electrical specifications * average current: 19 mA * max. current: 75 mA * DC supply: 3.3 V - 5.5 V Operation conditions * temperature: 0 – 50°C * humidity: 0 – 95 %RH * sensor lifetime: 15 years CO2-sensor: * NDIR CO 2 sensor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
